// Logisim project mul.circ as structural Verilog: 4 circuits, main circuit main
module main (
  input  [7:0] X,
  input  in_2,
  input  R
);

  wire and_1_out, and_2_out, and_3_out, and_4_out, and_5_out, and_6_out, and_7_out, and_8_out, ciso_1_out_3,
       clk_out, csadd_1_sum, csadd_2_sum, csadd_3_sum, csadd_4_sum, csadd_5_sum, csadd_6_sum, csadd_7_sum,
       main_1_out_5, undriven, undriven_2, undriven_3, undriven_4, undriven_5, undriven_6, undriven_7,
       undriven_8, undriven_9, undriven_10, undriven_11, undriven_12, undriven_13, undriven_14, undriven_15,
       undriven_16, undriven_17, undriven_18, undriven_19, undriven_20, undriven_21, undriven_22,
       undriven_23, undriven_24, undriven_25, undriven_26, undriven_27;
  wire [15:0] sipo_1_product;

  Clock clk (.out(clk_out));
  ciso ciso_1 (.SI(in_2), .CLK(clk_out), .out_3(ciso_1_out_3));
  and and_1 (and_1_out, ciso_1_out_3, X[7]);
  theTCMP_main main_1 (.A(and_1_out), .R(R), .out_5(main_1_out_5), .in_2(clk_out));  // open: out_4
  and and_2 (and_2_out, ciso_1_out_3, X[6]);
  CSADD csadd_1 (.Y(and_2_out), .X(main_1_out_5), .R(R), .sum(csadd_1_sum), .clk(clk_out));  // open: FDHA
  and and_3 (and_3_out, ciso_1_out_3, X[5]);
  and and_4 (and_4_out, ciso_1_out_3, X[4]);
  CSADD csadd_2 (.Y(and_3_out), .X(csadd_1_sum), .R(R), .sum(csadd_2_sum), .clk(clk_out));  // open: FDHA
  and and_5 (and_5_out, ciso_1_out_3, X[3]);
  and and_6 (and_6_out, ciso_1_out_3, X[2]);
  CSADD csadd_3 (.Y(and_4_out), .X(csadd_2_sum), .R(R), .sum(csadd_3_sum), .clk(clk_out));  // open: FDHA
  and and_7 (and_7_out, ciso_1_out_3, X[1]);
  and and_8 (and_8_out, ciso_1_out_3, X[0]);
  CSADD csadd_4 (.Y(and_5_out), .X(csadd_3_sum), .R(R), .sum(csadd_4_sum), .clk(clk_out));  // open: FDHA
  CSADD csadd_5 (.Y(and_6_out), .X(csadd_4_sum), .R(R), .sum(csadd_5_sum), .clk(clk_out));  // open: FDHA
  CSADD csadd_6 (.Y(and_7_out), .X(csadd_5_sum), .R(R), .sum(csadd_6_sum), .clk(clk_out));  // open: FDHA
  _7_Segment_Display u_7_segment_display_1 (
    .g(undriven_13), .f(undriven_19), .a(undriven_19), .b(undriven_12), .e(undriven_17), .d(undriven_18),
    .c(undriven_20));  // open: dp
  CSADD csadd_7 (.Y(and_8_out), .X(csadd_6_sum), .R(R), .sum(csadd_7_sum), .clk(clk_out));  // open: FDHA
  _7_Segment_Display u_7_segment_display_2 (
    .g(undriven_15), .f(undriven_14), .a(undriven_23), .b(undriven_11), .e(undriven_21), .d(undriven_22),
    .c(undriven_24));  // open: dp
  sipo sipo_1 (.SI(csadd_7_sum), .CLK(clk_out), .product(sipo_1_product));
  _7_Segment_Display u_7_segment_display_3 (
    .g(undriven_8), .f(undriven_16), .a(undriven_10), .b(undriven_9), .e(undriven_25), .d(undriven_26),
    .c(undriven_27));  // open: dp
  _7_Segment_Display u_7_segment_display_4 (
    .g(undriven_7), .f(undriven_6), .a(undriven), .b(undriven_2), .e(undriven_5), .d(undriven_4),
    .c(undriven_3));  // open: dp
endmodule

module ciso (
  input  SI,
  input  CLK,
  output out_3
);

  wire d_ff_1_q, d_ff_2_q, d_ff_3_q, d_ff_4_q, d_ff_5_q, d_ff_6_q, d_ff_7_q;

  D_Flip_Flop d_ff_1 (.D(SI), .clk(CLK), .Q(d_ff_1_q));  // open: Qn, preset, reset
  D_Flip_Flop d_ff_2 (.D(d_ff_1_q), .clk(CLK), .Q(d_ff_2_q));  // open: Qn, preset, reset
  D_Flip_Flop d_ff_3 (.D(d_ff_2_q), .clk(CLK), .Q(d_ff_3_q));  // open: Qn, preset, reset
  D_Flip_Flop d_ff_4 (.D(d_ff_3_q), .clk(CLK), .Q(d_ff_4_q));  // open: Qn, preset, reset
  D_Flip_Flop d_ff_5 (.D(d_ff_4_q), .clk(CLK), .Q(d_ff_5_q));  // open: Qn, preset, reset
  D_Flip_Flop d_ff_6 (.D(d_ff_5_q), .clk(CLK), .Q(d_ff_6_q));  // open: Qn, preset, reset
  D_Flip_Flop d_ff_7 (.D(d_ff_6_q), .clk(CLK), .Q(d_ff_7_q));  // open: Qn, preset, reset
  D_Flip_Flop d_ff_8 (.D(d_ff_7_q), .clk(CLK), .Q(out_3));  // open: Qn, preset, reset
endmodule

module sipo (
  input  SI,
  input  CLK,
  output [15:0] product
);

  D_Flip_Flop d_ff_1 (.D(SI), .clk(CLK), .Q(product[15]));  // open: Qn, preset, reset
  D_Flip_Flop d_ff_2 (.D(product[15]), .clk(CLK), .Q(product[14]));  // open: Qn, preset, reset
  D_Flip_Flop d_ff_3 (.D(product[14]), .clk(CLK), .Q(product[13]));  // open: Qn, preset, reset
  D_Flip_Flop d_ff_4 (.D(product[13]), .clk(CLK), .Q(product[12]));  // open: Qn, preset, reset
  D_Flip_Flop d_ff_5 (.D(product[12]), .clk(CLK), .Q(product[11]));  // open: Qn, preset, reset
  D_Flip_Flop d_ff_6 (.D(product[11]), .clk(CLK), .Q(product[10]));  // open: Qn, preset, reset
  D_Flip_Flop d_ff_7 (.D(product[10]), .clk(CLK), .Q(product[9]));  // open: Qn, preset, reset
  D_Flip_Flop d_ff_8 (.D(product[9]), .clk(CLK), .Q(product[8]));  // open: Qn, preset, reset
  D_Flip_Flop d_ff_9 (.D(product[8]), .clk(CLK), .Q(product[7]));  // open: Qn, preset, reset
  D_Flip_Flop d_ff_10 (.D(product[7]), .clk(CLK), .Q(product[6]));  // open: Qn, preset, reset
  D_Flip_Flop d_ff_11 (.D(product[6]), .clk(CLK), .Q(product[5]));  // open: Qn, preset, reset
  D_Flip_Flop d_ff_12 (.D(product[5]), .clk(CLK), .Q(product[4]));  // open: Qn, preset, reset
  D_Flip_Flop d_ff_13 (.D(product[4]), .clk(CLK), .Q(product[3]));  // open: Qn, preset, reset
  D_Flip_Flop d_ff_14 (.D(product[3]), .clk(CLK), .Q(product[2]));  // open: Qn, preset, reset
  D_Flip_Flop d_ff_15 (.D(product[2]), .clk(CLK), .Q(product[1]));  // open: Qn, preset, reset
  D_Flip_Flop d_ff_16 (.D(product[1]), .clk(CLK), .Q(product[0]));  // open: Qn, preset, reset
endmodule

module loader (
  input  rst,
  input  serialIn,
  output [15:0] parallelOut
);

  wire clk_out, counter_1_carry, d_ff_1_q, not_1_out, or_1_out;
  wire [15:0] shift_register_1_p5;

  not not_1 (not_1_out, d_ff_1_q);
  Clock clk (.out(clk_out));
  // Shift_Register #(.length(16)) shift_register_1: pin names not known; wires that end beside it: rst, not_1_out, serialIn, clk_out, shift_register_1_p5[0], shift_register_1_p5[1], shift_register_1_p5[2], shift_register_1_p5[3], shift_register_1_p5[4], shift_register_1_p5[5], shift_register_1_p5[6], shift_register_1_p5[7], shift_register_1_p5[8], shift_register_1_p5[9], shift_register_1_p5[10], shift_register_1_p5[11]
  Multiplexer #(.width(16)) multiplexer_1 (
    .in0({16{1'b0}}), .in1(shift_register_1_p5), .out(parallelOut), .sel(d_ff_1_q));
  Counter #(.max('hf), .width(4)) counter_1 (
    .up(1'b1), .clk(clk_out), .carry(counter_1_carry));  // open: clr, load, count, D, Q
  or or_1 (or_1_out, d_ff_1_q, counter_1_carry);
  D_Flip_Flop d_ff_1 (.D(or_1_out), .clk(clk_out), .Q(d_ff_1_q), .reset(rst));  // open: Qn, preset
endmodule
